# Fritzing sketch Scheme (saved by Fritzing 0.9.4)
breadboards: 1

parts:
  U1 = NodeMCU V3.0
  R1 = Resistor [tolerance=±5% resistance=2.2k package=THT]
  Q1 = NPN-Transistor [package="TO92 [THT]"]
  M1 = DC Motor
  VCC1 = 4 x AAA Battery Mount
  U2 = RELAY [package=relay-g5q]
  S1 = Pushbutton [package="[THT]"]
  AM1 = AM2320 Humidity and Temperature Sensor [part_number="Adafruit #3721"]
  R2 = Resistor [tolerance=±5% resistance=330 package=THT]
  LED1 = LED - 5mm [color="Red (633nm)" package="5 mm [THT]"]
  D1 = Rectifier Diode [part_number=1N4001 package="300 mil [THT]"]
  R3 = Resistor [tolerance=±5% resistance=100 package=THT]
  R4 = Resistor [tolerance=±5% resistance=10k package=THT]
  C1 = Ceramic Capacitor [capacitance=100nF package="100 mil [THT, multilayer]"]
  Part1 = Soil Moisture Sensor
  LED2 = LED - 5mm [color="Green (555nm)" package="5 mm [THT]"]
  R5 = Resistor [tolerance=±5% resistance=330 package=THT]

nets:
  N1: U1.D0, U1.D1, AM1.SCL
  N2: U1.D2, AM1.SDA
  N3: U1.D5, R5.Pin_0
  N4: U1.D6, R3.Pin_1, R4.Pin_0, C1.0
  N5: U1.D7, R1.Pin_1, R2.Pin_0
  N6: U1.D8, Part1.VCC
  GND: U1.TX, U1.GND, Q1.E, AM1.GND, LED1.cathode, R4.Pin_1, C1.1, Part1.GND, LED2.cathode
  3V3: U1.3V3, U2.COIL1, S1.Pin_1, S1.Pin_2, AM1.VDD, D1.cathode
  N7: U1.A0, Part1.SIG
  N8: R1.Pin_0, Q1.B
  N9: Q1.C, U2.COIL2, D1.anode
  N10: M1.pin_1, VCC1.-
  N11: M1.pin_2, U2.NO
  N12: VCC1.+, U2.MAIN
  N13: S1.Pin_3, S1.Pin_4, R3.Pin_0
  N14: R2.Pin_1, LED1.anode
  N15: LED2.anode, R5.Pin_1

custom parts:
  NodeMCU V3.0: NodeMcu V3 Lua WIFI Development Board
  AM2320 Humidity and Temperature Sensor: AM2320 I2C Humidity and Temperature Sensor
