# Fritzing sketch Scheme (saved by Fritzing 0.9.3b)
breadboards: 1

parts:
  AM1 = AM2320 Humidity and Temperature Sensor [part_number="Adafruit #3721"]
  U1 = NodeMCU V3.0

nets:
  VDD: AM1.VDD, U1.3V3
  N1: AM1.SDA, U1.D2
  GND: AM1.GND, U1.TX, U1.GND
  N2: AM1.SCL, U1.D0, U1.D1

custom parts:
  AM2320 Humidity and Temperature Sensor: AM2320 I2C Humidity and Temperature Sensor
  NodeMCU V3.0: NodeMcu V3 Lua WIFI Development Board
